# Fritzing sketch banana (saved by Fritzing 0.9.4)
circuit board: 8.46667cm x 5.64444cm
breadboards: 1

parts:
  S1 = 9-pin-tube-socket
  C5 = Electrolytic Capacitor [capacitance=1µF package="100 mil [THT, electrolytic]"]
  12V = female pin header, 2 pins [form="♀ (female)"]
  OUT = Audio Jack (TRS) 3.5mm [package="4Ucon 08780 [THT]"]
  R10 = Resistor [tolerance=±5% resistance=220 package=THT]
  IN = Audio Jack (TRS) 3.5mm [package="4Ucon 08780 [THT]"]
  C4 = Electrolytic Capacitor [capacitance=1µF package="100 mil [THT, electrolytic]"]
  S1a = female pin header, 1 pin [form="♀ (female)"]
  R5 = Resistor [tolerance=±5% resistance=220 package=THT]
  LED1 = LED - 5mm [color="Red (633nm)" package="5 mm [THT]"]
  R9 = Resistor [tolerance=±5% resistance=220 package=THT]
  R4 = Resistor [tolerance=±5% resistance=220 package=THT]
  R2 = Resistor [tolerance=±5% resistance=220 package=THT]
  R3 = Resistor [tolerance=±5% resistance=220 package=THT]
  C1 = Ceramic Capacitor [capacitance=100nF package="200 mil [THT, multilayer]"]
  R6 = Resistor [tolerance=±5% resistance=220 package=THT]
  R8 = Resistor [tolerance=±5% resistance=220 package=THT]
  C2 = Ceramic Capacitor [capacitance=100nF package="200 mil [THT, multilayer]"]
  C3 = Electrolytic Capacitor [capacitance=1µF package="100 mil [THT, electrolytic]"]
  R1 = Resistor [tolerance=±5% resistance=220 package=THT]
  P1 = Rotary Potentiometer (Large) [maximum_resistance=100kΩ package=THT]
  S2 = female pin header, 2 pins [form="♀ (female)"]

nets:
  N1: S1.pin_1, R8.Pin_0, C2.1
  N2: S1.pin_2, C1.1, R6.Pin_0
  N3: S1.pin_3, S1.pin_5, C5.-, 12V.pin2, OUT.Sleeve, IN.Sleeve, C4.-, R9.Pin_1, R4.Pin_1, R2.Pin_1, R6.Pin_1, P1.leg2, S2.pin2
  N4: S1.pin_4, C5.+, 12V.pin1, R10.Pin_1
  N5: S1.pin_6, R3.Pin_0, C1.0
  N6: S1.pin_7, R1.Pin_0
  N7: S1.pin_8, R4.Pin_0, C3.+
  N8: OUT.Ring, S1a.pin1
  N9: R10.Pin_0, C4.+, R5.Pin_0, R3.Pin_1, R8.Pin_1
  N10: R5.Pin_1, LED1.cathode
  N11: R9.Pin_0, C3.-, S2.pin1
  N12: R2.Pin_0, R1.Pin_1
  N13: C2.0, P1.leg1

custom parts:
  9-pin-tube-socket: 9 pin tube socket.
